# Fritzing sketch diagram (saved by Fritzing 1.0.2b)
circuit board: 8.46667cm x 5.64444cm

parts:
  M1 = DOIT Esp32 DevKit v1 (30 pins long, 11 pins width) [part_number=ESP32S-PIN30]
  M2 = DC Motor [voltage_(max)=6V voltage_(min)=3V]
  S1 = H-Bridge with L298N
  BATT1 = LiPoly Battery (1300mAh)
  M4 = DC Motor [voltage_(max)=6V voltage_(min)=3V]
  M6 = DC Motor [voltage_(max)=6V voltage_(min)=3V]
  M5 = DC Motor [voltage_(max)=6V voltage_(min)=3V]
  L1 = Inductor [package="400 mil [THT]"]  # not connected

nets:
  GND: M1.GND, S1.GND, BATT1.negative
  N1: M1.D32, S1.ENB
  N2: M1.D33, S1.IN4
  N3: M1.D25, S1.IN3
  N4: M1.D26, S1.IN2
  N5: M1.D27, S1.IN1
  N6: M1.D14, M1.D12, S1.ENA
  VIN: M1.VIN, S1.5V
  N7: M2.pin_1, S1.M2-02, M4.pin_1
  N8: M2.pin_2, S1.M2-01, M4.pin_2
  N9: S1.12V, BATT1.positive
  N10: S1.M1-01, M6.pin_2, M5.pin_2
  N11: S1.M1-02, M6.pin_1, M5.pin_1

custom parts:
  DOIT Esp32 DevKit v1 (30 pins long, 11 pins width): The DOIT Esp32 DevKit v1 is one of the development board created by DOIT to evaluate the ESP-WROOM-32 module. It is based on the ESP32 microcontroller that boasts Wifi, Bluetooth, Ethernet and Low Power support all in a single chip. (vanepp) made breadboard work, adjusted pin numbering and labels and reduced size of schematic and cleaned up pcb. This chip is 30pins long (2 x15) and 11 pins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
  H-Bridge with L298N: h-bridge
  LiPoly Battery (1300mAh): Lithium Ion Polymer Battery (1300mAh)
